# Fritzing sketch breadboard_schema (saved by Fritzing 0.9.2b)
breadboards: 1

parts:
  Part1 = Arduino Uno (Rev3)
  IC1 = H-Bridge [package=THT]  # not connected
  BAT1 = BC9VPC [package=bc9vpc]
  M4 = DC Motor  # not connected
  Part2 = SRF05 Ultrasonic Rangefinder
  M5 = DC Motor  # not connected
  Part3 = Bluetooth HC-06

nets:
  N1: Part1.D9_PWM, Part3.RXD
  N2: Part1.D10_PWM/SS, Part3.TXD
  N3: Part1.D11_PWM/MOSI, Part2.Trig
  N4: Part1.D12/MISO, Part2.Echo
  GND: Part1.GND, BAT1.V-, Part2.GND, Part3.GND
  VCC: Part1.5V, Part2.VCC, Part3.VCC
